# Fritzing sketch schematic (saved by Fritzing 0.9.4)
breadboards: 1

parts:
  faucet1 = SWITCH-MOMENTARY-2 [package=tactile-pth-12mm]
  faucet2 = SWITCH-MOMENTARY-2 [package=tactile-pth-12mm]
  faucet3 = SWITCH-MOMENTARY-2 [package=tactile-pth-12mm]
  Arduino = Arduino Pro Mini v13
  R1 = Resistor [tolerance=±5% resistance=470 package="0603 [SMD]"]
  U1 = TRANSISTOR_NPN_2 [part_number=2N3904 package=to-92]
  U2 = RELAY [package=relay-t9a-2]
  to_the_water_purifier = Header 5x2 [package=2x5-shrouded_smd]
  U4 = RELAY [package=relay-t9a-2]
  U6 = RELAY [package=relay-t9a-2]
  R2 = Resistor [tolerance=±5% resistance=470 package="0603 [SMD]"]
  U3 = TRANSISTOR_NPN_2 [part_number=2N3904 package=to-92]
  R3 = Resistor [tolerance=±5% resistance=470 package="0603 [SMD]"]
  U5 = TRANSISTOR_NPN_2 [part_number=2N3904 package=to-92]

nets:
  N1: faucet1.1, Arduino.D10_PWM/SS
  N2: faucet1.2, faucet2.2, faucet3.2, Arduino.GND, U1.E, U3.E, U5.E
  N3: faucet2.1, Arduino.D11_PWM/MOSI
  N4: faucet3.1, Arduino.D12/MISO
  N5: Arduino.VCC, U2.COIL2, U4.COIL2, U6.COIL2
  N6: Arduino.D9_PWM, R1.Pin_0
  N7: Arduino.D8, R2.Pin_0
  N8: Arduino.D7, R3.Pin_0
  N9: R1.Pin_1, U1.B
  N10: U1.C, U2.COIL1
  N11: U2.MAIN, to_the_water_purifier.1, U4.MAIN, U6.MAIN
  N12: U2.NO, to_the_water_purifier.5
  N13: to_the_water_purifier.7, U4.NO
  N14: to_the_water_purifier.9, U6.NO
  N15: U4.COIL1, U3.C
  N16: U6.COIL1, U5.C
  N17: R2.Pin_1, U3.B

notes:
  these use the ino's internal pull-up resistors, no need for external resistors
